# Fritzing sketch Handy (saved by Fritzing 0.9.3b)

parts:
  Part1 = Adafruit Feather M0 Bluefruit LE [part_number="Adafruit #2995"]
  Part2 = Adafruit DC+Stepper FeatherWing [part_number="Adafruit #2927"]
  Stepdown_Voltage1 = Polulu Stepdown Voltage [part_number=D24V25F3,D24V25F5]
  BATT2 = LiPoly Battery (1300mAh)
  MOTOR1 = Adafruit Gear-Reduced Stepper Motor (small)
  MOTOR2 = Adafruit Gear-Reduced Stepper Motor (small)
  MOTOR3 = Adafruit Gear-Reduced Stepper Motor (small)
  MOTOR4 = Adafruit Gear-Reduced Stepper Motor (small)
  U2 = LM2621 [package=msop-8]
  U3 = TOUCH [package=touch2]  # not connected
  U4 = TOUCH [package=touch2]  # not connected
  R1 = Resistor [tolerance=±5% resistance=220 package=THT]
  R2 = Resistor [tolerance=±5% resistance=220 package=THT]

nets:
  N1: Part1.A5, R1.Pin_1
  N2: Part1.A3, MOTOR2.BLUE
  N3: Part1.A2, MOTOR3.BLUE
  N4: Part1.A1, MOTOR4.BLUE
  N5: Part1.A0, MOTOR1.BLUE
  GND: Part1.GND, Part2.GND, MOTOR1.PINK, MOTOR2.PINK, MOTOR3.PINK, MOTOR4.PINK, U2.BOOT
  +3V3: Part1.+3V3, Part2.+3.3V, Stepdown_Voltage1.VOut, MOTOR1.RED, MOTOR2.RED, MOTOR3.RED, MOTOR4.RED
  N6: Part1.SCL, Part2.SCL
  N7: Part1.SDA, Part2.SDA
  N8: Part2.VMOTOR, U2.VDD
  N9: Stepdown_Voltage1.VIn, BATT2.positive, U2.FREQ
  N10: Stepdown_Voltage1.GND#2, R1.Pin_0, R2.Pin_1
  N11: Stepdown_Voltage1.GND#3, BATT2.negative, U2.EN

custom parts:
  Adafruit Feather M0 Bluefruit LE: This is the Adafruit Feather M0 Bluefruit LE - our take on an 'all-in-one' Arduino-compatible + Bluetooth Low Energy with built in USB and battery charging. Its an Adafruit Feather M0 with a BTLE module, ready to rock! We have other boards in the Feather family, check'em out here. Bluetooth Low Energy is the hottest new low-power, 2.4GHz spectrum wireless protocol. In particular, its the only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
  Adafruit DC+Stepper FeatherWing: This is the DC Motor + Stepper FeatherWing which will let you use 2 x bi-polar stepper motors or 4 x brushed DC motorx (or 1 stepper and 2 DC motors). Using our Feather Stacking Headers or Feather Female Headers you can connect a FeatherWing on top or bottom of your Feather board and let the board take flight! The original Adafruit Motorshield Kit is one of our most beloved kits, which is why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
  Polulu Stepdown Voltage: Polulu Stepdown Voltage 3V3 or 5V, 2.5A
  LiPoly Battery (1300mAh): Lithium Ion Polymer Battery (1300mAh)
  Adafruit Gear-Reduced Stepper Motor (small): Adafruit gear-reduction stepper motor (small)
